# Fritzing sketch Rubik's Cube Solver - Stepper Motor Board (saved by Fritzing 0.9.4)
stripboards: 1

parts:
  J1 = Screw terminal - 2 pins [package=THT]
  Part1 = Arduino Uno (Rev3)
  DRV_1 = DRV 8825 Stepper Motor Carrier, High Current [part_number="DRV 8825"]  # not connected
  J2 = Screw terminal - 2 pins [package=THT]
  DRV_2 = DRV 8825 Stepper Motor Carrier, High Current [part_number="DRV 8825"]  # not connected
  DRV_3 = DRV 8825 Stepper Motor Carrier, High Current [part_number="DRV 8825"]  # not connected
  DRV_5 = DRV 8825 Stepper Motor Carrier, High Current [part_number="DRV 8825"]  # not connected
  DRV_6 = DRV 8825 Stepper Motor Carrier, High Current [part_number="DRV 8825"]  # not connected
  Power_plug1 = Power plug
  M1 = Stepper Motor - Bipolar  # not connected
  M2 = Stepper Motor - Bipolar  # not connected
  M3 = Stepper Motor - Bipolar  # not connected
  M4 = Stepper Motor - Bipolar  # not connected
  M5 = Stepper Motor - Bipolar  # not connected
  M6 = Stepper Motor - Bipolar  # not connected
  DRV_4 = DRV 8825 Stepper Motor Carrier, High Current [part_number="DRV 8825"]  # not connected
  C1 = Electrolytic Capacitor [capacitance=100µF voltage=50V package="200 mil [THT, electrolytic]"]
  C2 = Electrolytic Capacitor [capacitance=100µF voltage=50V package="200 mil [THT, electrolytic]"]
  C3 = Electrolytic Capacitor [capacitance=100µF voltage=50V package="200 mil [THT, electrolytic]"]
  C4 = Electrolytic Capacitor [capacitance=100µF voltage=50V package="200 mil [THT, electrolytic]"]
  C5 = Electrolytic Capacitor [capacitance=100µF voltage=50V package="200 mil [THT, electrolytic]"]
  C6 = Electrolytic Capacitor [capacitance=100µF voltage=50V package="200 mil [THT, electrolytic]"]
  J3 = female pin header, 4 pins [form="♀ (female)"]  # not connected
  J4 = female pin header, 4 pins [form="♀ (female)"]  # not connected
  J5 = female pin header, 4 pins [form="♀ (female)"]  # not connected
  J6 = female pin header, 4 pins [form="♀ (female)"]  # not connected
  J7 = female pin header, 4 pins [form="♀ (female)"]  # not connected
  J8 = female pin header, 4 pins [form="♀ (female)"]  # not connected
  J9 = female pin header, 2 pins [form="♀ (female)"]  # not connected
  J10 = female pin header, 2 pins [form="♀ (female)"]  # not connected
  J11 = female pin header, 2 pins [form="♀ (female)"]  # not connected
  J12 = female pin header, 2 pins [form="♀ (female)"]  # not connected
  J13 = female pin header, 2 pins [form="♀ (female)"]  # not connected
  J14 = female pin header, 2 pins [form="♀ (female)"]  # not connected

nets:
  N1: J1.pin1, Power_plug1.VCC, C1.-, C2.-, C3.-, C4.-, C5.-, C6.-
  N2: J1.pin2, Power_plug1.GND, C1.+, C2.+, C3.+, C4.+, C5.+, C6.+
  N3: Part1.5V, J2.pin2
  N4: Part1.GND, J2.pin1

// code stored in the sketch: Untitled.ino

